# Fritzing sketch breadboard (saved by Fritzing 0.9.3b)
breadboards: 1

parts:
  Part1 = Arduino Uno (Rev3)
  J1 = Piezo Speaker
  hc-sr1 = hc-sr04

nets:
  N1: Part1.D9_PWM, J1.pin2
  GND: Part1.GND, J1.pin1, hc-sr1.GND
  N2: Part1.D2, hc-sr1.Trig
  N3: Part1.D3_PWM, hc-sr1.Echo
  5V: Part1.5V, hc-sr1.VCC

custom parts:
  hc-sr04: This is a HC-SR04 Distance Sensor
